// Logisim project RV32I_base.circ as structural Verilog: 8 circuits, main circuit RegisterFile
module main (
  input  [31:0] in_1,
  input  [31:0] INST,
  output [31:0] out_3
);

  wire ALUSrcA, ALUSrcB, BrEq, BrLT, BrUn, clk, PCSel, RegWrite;
  wire [1:0] WBSel;
  wire [3:0] ALUOp, MemRW;
  wire [5:0] ImmSrc;
  wire [31:0] adder_1_out, alu_1_out_4, d_mem_1_out_5, immgen_1_out_3, multiplexer_1_out, multiplexer_2_out,
       multiplexer_3_out, register_1_q, registerfile_1_data_a, registerfile_1_data_b;

  Multiplexer #(.width(32), .enable("false")) multiplexer_1 (
    .in0(adder_1_out), .in1(alu_1_out_4), .out(multiplexer_1_out), .sel(PCSel));
  Register #(.width(32)) register_1 (.D(multiplexer_1_out), .en(1'b1), .clk(clk), .Q(register_1_q), .clr(1'b0));
  Clock clock_1 (.out(clk));
  I_MEM i_mem_1 (.in_1(register_1_q));  // open: out_2
  Adder #(.width(32)) adder_1 (.a(register_1_q), .b(32'h4), .out(adder_1_out), .cin(1'b0));  // open: cout
  ControlUnit controlunit_1 (
    .in_1(INST), .RegWrite(RegWrite), .ALUSrcA(ALUSrcA), .ALUSrcB(ALUSrcB), .ALUOp(ALUOp), .WBSel(WBSel),
    .PCSel(PCSel), .ImmSrc(ImmSrc), .MemRW(MemRW), .BrEq(BrEq), .BrLT(BrLT), .BrUn(BrUn));
  RegisterFile registerfile_1 (
    .DATA_A(registerfile_1_data_a), .DATA_B(registerfile_1_data_b), .ADDR_IN(INST[11:7]), .DATA_IN(out_3),
    .LOAD(RegWrite), .ADDR_A(INST[19:15]), .ADDR_B(INST[24:20]), .CLK(clk));
  ImmGen immgen_1 (.in_2(INST[31:7]), .out_3(immgen_1_out_3), .in_1(ImmSrc));
  BranchCom branchcom_1 (
    .in_1(registerfile_1_data_a), .in_2(registerfile_1_data_b), .BrEq(BrEq), .BrLT(BrLT), .BrUn(BrUn));
  ALU alu_1 (.in_2(multiplexer_2_out), .in_3(multiplexer_3_out), .in_1(ALUOp), .out_4(alu_1_out_4));
  Multiplexer #(.width(32), .enable("false")) multiplexer_2 (
    .in0(registerfile_1_data_a), .in1(register_1_q), .out(multiplexer_2_out), .sel(ALUSrcA));
  Multiplexer #(.width(32), .enable("false")) multiplexer_3 (
    .in0(registerfile_1_data_b), .in1(in_1), .out(multiplexer_3_out), .sel(ALUSrcB));
  D_MEM d_mem_1 (.in_3(clk), .in_4(registerfile_1_data_b), .out_5(d_mem_1_out_5), .in_2(alu_1_out_4), .in_1(MemRW));
  Multiplexer #(.select(2), .width(32), .enable("false")) multiplexer_4 (
    .in0(d_mem_1_out_5), .in1(alu_1_out_4), .in2(adder_1_out), .out(out_3), .sel(WBSel));  // open: in3
endmodule

module ControlUnit (
  input  [31:0] in_1,
  input  BrEq,
  input  BrLT,
  output [3:0] ALUOp,
  output [3:0] MemRW,
  output BrUn,
  output RegWrite,
  output ALUSrcA,
  output ALUSrcB,
  output [1:0] WBSel,
  output [5:0] ImmSrc,
  output PCSel
);

  wire and_1_out, and_2_out, and_3_out, and_4_out, and_5_out, and_7_out, and_11_out, and_12_out, and_15_out,
       and_16_out, and_17_out, and_18_out, and_19_out, bitselector_1_out, not_1_out, not_2_out, not_3_out,
       not_4_out, not_5_out, not_6_out, not_7_out, not_8_out, not_9_out, not_10_out, not_11_out, not_12_out,
       not_13_out, not_14_out, not_15_out, not_16_out, not_17_out, not_18_out, not_19_out, not_20_out,
       not_21_out, not_22_out, not_23_out, not_24_out, or_2_out, or_5_out, or_10_out;
  wire [2:0] multiplexer_1_out;

  not not_1 (not_1_out, in_1[6]);
  not not_2 (not_2_out, in_1[3]);
  not not_3 (not_3_out, in_1[2]);
  not not_4 (not_4_out, in_1[6]);
  not not_5 (not_5_out, in_1[5]);
  not not_6 (not_6_out, in_1[3]);
  not not_7 (not_7_out, in_1[2]);
  not not_8 (not_8_out, in_1[6]);
  not not_9 (not_9_out, in_1[5]);
  not not_10 (not_10_out, in_1[4]);
  not not_11 (not_11_out, in_1[3]);
  not not_12 (not_12_out, in_1[2]);
  not not_13 (not_13_out, in_1[6]);
  not not_14 (not_14_out, in_1[4]);
  not not_15 (not_15_out, in_1[3]);
  not not_16 (not_16_out, in_1[2]);
  not not_17 (not_17_out, in_1[4]);
  not not_18 (not_18_out, in_1[3]);
  not not_19 (not_19_out, in_1[4]);
  not not_20 (not_20_out, in_1[4]);
  not not_21 (not_21_out, in_1[3]);
  not not_22 (not_22_out, in_1[2]);
  not not_23 (not_23_out, in_1[6]);
  not not_24 (not_24_out, in_1[3]);
  and and_1 (and_1_out, not_1_out, in_1[5], in_1[4], not_2_out, not_3_out);
  and and_2 (and_2_out, not_4_out, not_5_out, in_1[4], not_6_out, not_7_out);
  and and_3 (and_3_out, in_1[14], ~in_1[13], in_1[12]);  // AND_Gate
  and and_4 (and_4_out, ~in_1[14], ~in_1[13], in_1[12]);  // AND_Gate
  and and_5 (and_5_out, not_8_out, not_9_out, not_10_out, not_11_out, not_12_out);
  and and_6 (ImmSrc[3], not_13_out, in_1[5], not_14_out, not_15_out, not_16_out);
  and and_7 (and_7_out, in_1[6], in_1[5], not_17_out, not_18_out, in_1[2]);
  and and_8 (ImmSrc[2], in_1[6], in_1[5], not_19_out, in_1[3], in_1[2]);
  and and_9 (ImmSrc[1], in_1[6], in_1[5], not_20_out, not_21_out, not_22_out);
  and and_10 (ImmSrc[0], not_23_out, in_1[4], not_24_out, in_1[2]);
  or or_1 (RegWrite, and_1_out, and_2_out, and_5_out, ImmSrc[0], and_7_out, ImmSrc[2]);
  or or_2 (or_2_out, and_3_out, and_4_out);
  and and_11 (and_11_out, in_1[5], ImmSrc[0]);
  and and_12 (and_12_out, ImmSrc[0], ~in_1[5]);  // AND_Gate
  or or_3 (ALUSrcA, and_7_out, ImmSrc[2], ImmSrc[1], and_12_out);
  or or_4 (ALUSrcB, and_2_out, and_5_out, ImmSrc[3], and_7_out, ImmSrc[2], ImmSrc[1], ImmSrc[0]);
  Multiplexer #(.width(3), .enable("false")) multiplexer_1 (
    .in0(in_1[14:12]), .in1(3'b000), .out(multiplexer_1_out), .sel(or_5_out));
  or or_5 (or_5_out, and_5_out, ImmSrc[3], and_7_out, ImmSrc[2], ImmSrc[1]);
  Multiplexer #(.width(4), .enable("false")) multiplexer_2 (
    .in0({in_1[30], multiplexer_1_out}), .in1(4'b1001), .out(ALUOp), .sel(and_11_out));
  or or_6 (WBSel[0], and_5_out, ImmSrc[0]);
  or or_7 (WBSel[1], ImmSrc[2], and_7_out);
  or or_8 (ImmSrc[5], and_2_out, and_5_out, and_7_out);
  and and_13 (ImmSrc[4], and_2_out, or_2_out);
  and and_14 (BrUn, bitselector_1_out, ImmSrc[1]);
  BitSelector #(.width(3)) bitselector_1 (.in(in_1[14:12]), .out(bitselector_1_out), .sel(2'b01));
  or or_9 (PCSel, and_7_out, ImmSrc[2], and_15_out);
  and and_15 (and_15_out, ImmSrc[1], or_10_out);
  and and_16 (and_16_out, ~in_1[14], ~in_1[12], BrEq);  // AND_Gate
  or or_10 (or_10_out, and_16_out, and_17_out, and_18_out, and_19_out);
  and and_17 (and_17_out, ~in_1[14], in_1[12], ~BrEq);  // AND_Gate
  and and_18 (and_18_out, in_1[14], ~in_1[12], BrLT);  // AND_Gate
  and and_19 (and_19_out, in_1[14], in_1[12], ~BrLT);  // AND_Gate

  assign MemRW = {ImmSrc[3], in_1[14:12]};

  // Notes on the sheet:
  //   WBSel: pull=down
  //   MemRW: pull=down
  //   ImmSrc: pull=down
  //   ALUSrcB: pull=down
  //   ALUOp: pull=down
  //   R_Type
  //   Reg I_Type
  //   Decode for SRAI,SRLI,SLLI
  //   Mem I_Type (Load)
  //   S_Type (Store)
  //   JALR
  //   J_Type
  //   B_Type
  //   U_Type
endmodule

module RegisterFile (
  input  [31:0] DATA_IN,
  input  CLK,
  input  LOAD,
  input  [4:0] ADDR_IN,
  input  [4:0] ADDR_A,
  input  [4:0] ADDR_B,
  output [31:0] DATA_A,
  output [31:0] DATA_B
);

  wire and_1_out, and_2_out, and_3_out, and_4_out, and_5_out, and_6_out, and_7_out, and_8_out, and_9_out,
       and_10_out, and_11_out, and_12_out, and_13_out, and_14_out, and_15_out, and_16_out, and_17_out,
       and_18_out, and_19_out, and_20_out, and_21_out, and_22_out, and_23_out, and_24_out, and_25_out,
       and_26_out, and_27_out, and_28_out, and_29_out, and_30_out, and_31_out, and_32_out, decoder_1_out0,
       decoder_1_out1, decoder_1_out2, decoder_1_out3, decoder_1_out4, decoder_1_out5, decoder_1_out6,
       decoder_1_out7, decoder_1_out8, decoder_1_out9, decoder_1_out10, decoder_1_out11, decoder_1_out12,
       decoder_1_out13, decoder_1_out14, decoder_1_out15, decoder_1_out16, decoder_1_out17, decoder_1_out18,
       decoder_1_out19, decoder_1_out20, decoder_1_out21, decoder_1_out22, decoder_1_out23, decoder_1_out24,
       decoder_1_out25, decoder_1_out26, decoder_1_out27, decoder_1_out28, decoder_1_out29, decoder_1_out30,
       decoder_1_out31;
  wire [31:0] register_1_q, register_2_q, register_3_q, register_4_q, register_5_q, register_6_q,
       register_7_q, register_8_q, register_9_q, register_10_q, register_11_q, register_12_q, register_13_q,
       register_14_q, register_15_q, register_16_q, register_17_q, register_18_q, register_19_q,
       register_20_q, register_21_q, register_22_q, register_23_q, register_24_q, register_25_q,
       register_26_q, register_27_q, register_28_q, register_29_q, register_30_q, register_31_q,
       register_32_q;

  Decoder #(.select(5), .enable("false")) decoder_1 (
    .out0(decoder_1_out0), .out1(decoder_1_out1), .out2(decoder_1_out2), .out3(decoder_1_out3),
    .out4(decoder_1_out4), .out5(decoder_1_out5), .out6(decoder_1_out6), .out7(decoder_1_out7),
    .out8(decoder_1_out8), .out9(decoder_1_out9), .out10(decoder_1_out10), .out11(decoder_1_out11),
    .out12(decoder_1_out12), .out13(decoder_1_out13), .out14(decoder_1_out14), .out15(decoder_1_out15),
    .out16(decoder_1_out16), .out17(decoder_1_out17), .out18(decoder_1_out18), .out19(decoder_1_out19),
    .out20(decoder_1_out20), .out21(decoder_1_out21), .out22(decoder_1_out22), .out23(decoder_1_out23),
    .out24(decoder_1_out24), .out25(decoder_1_out25), .out26(decoder_1_out26), .out27(decoder_1_out27),
    .out28(decoder_1_out28), .out29(decoder_1_out29), .out30(decoder_1_out30), .out31(decoder_1_out31),
    .sel(ADDR_IN));
  Register #(.width(32)) register_1 (.D({32{1'b0}}), .en(and_1_out), .clk(CLK), .Q(register_1_q), .clr(1'b0));
  and and_1 (and_1_out, LOAD, decoder_1_out0);
  Register #(.width(32)) register_2 (.D(DATA_IN), .en(and_2_out), .clk(CLK), .Q(register_2_q), .clr(1'b0));
  and and_2 (and_2_out, LOAD, decoder_1_out1);
  Register #(.width(32)) register_3 (.D(DATA_IN), .en(and_3_out), .clk(CLK), .Q(register_3_q), .clr(1'b0));
  and and_3 (and_3_out, LOAD, decoder_1_out2);
  Register #(.width(32)) register_4 (.D(DATA_IN), .en(and_4_out), .clk(CLK), .Q(register_4_q), .clr(1'b0));
  and and_4 (and_4_out, LOAD, decoder_1_out3);
  Register #(.width(32)) register_5 (.D(DATA_IN), .en(and_5_out), .clk(CLK), .Q(register_5_q), .clr(1'b0));
  and and_5 (and_5_out, LOAD, decoder_1_out4);
  Register #(.width(32)) register_6 (.D(DATA_IN), .en(and_6_out), .clk(CLK), .Q(register_6_q), .clr(1'b0));
  and and_6 (and_6_out, LOAD, decoder_1_out5);
  Register #(.width(32)) register_7 (.D(DATA_IN), .en(and_7_out), .clk(CLK), .Q(register_7_q), .clr(1'b0));
  and and_7 (and_7_out, LOAD, decoder_1_out6);
  Register #(.width(32)) register_8 (.D(DATA_IN), .en(and_8_out), .clk(CLK), .Q(register_8_q), .clr(1'b0));
  and and_8 (and_8_out, LOAD, decoder_1_out7);
  Register #(.width(32)) register_9 (.D(DATA_IN), .en(and_9_out), .clk(CLK), .Q(register_9_q), .clr(1'b0));
  and and_9 (and_9_out, LOAD, decoder_1_out8);
  Register #(.width(32)) register_10 (.D(DATA_IN), .en(and_10_out), .clk(CLK), .Q(register_10_q), .clr(1'b0));
  and and_10 (and_10_out, LOAD, decoder_1_out9);
  Register #(.width(32)) register_11 (.D(DATA_IN), .en(and_11_out), .clk(CLK), .Q(register_11_q), .clr(1'b0));
  and and_11 (and_11_out, LOAD, decoder_1_out10);
  Register #(.width(32)) register_12 (.D(DATA_IN), .en(and_12_out), .clk(CLK), .Q(register_12_q), .clr(1'b0));
  and and_12 (and_12_out, LOAD, decoder_1_out11);
  Register #(.width(32)) register_13 (.D(DATA_IN), .en(and_13_out), .clk(CLK), .Q(register_13_q), .clr(1'b0));
  and and_13 (and_13_out, LOAD, decoder_1_out12);
  Register #(.width(32)) register_14 (.D(DATA_IN), .en(and_14_out), .clk(CLK), .Q(register_14_q), .clr(1'b0));
  and and_14 (and_14_out, LOAD, decoder_1_out13);
  Register #(.width(32)) register_15 (.D(DATA_IN), .en(and_15_out), .clk(CLK), .Q(register_15_q), .clr(1'b0));
  and and_15 (and_15_out, LOAD, decoder_1_out14);
  Register #(.width(32)) register_16 (.D(DATA_IN), .en(and_16_out), .clk(CLK), .Q(register_16_q), .clr(1'b0));
  and and_16 (and_16_out, LOAD, decoder_1_out15);
  Register #(.width(32)) register_17 (.D(DATA_IN), .en(and_17_out), .clk(CLK), .Q(register_17_q), .clr(1'b0));
  and and_17 (and_17_out, LOAD, decoder_1_out16);
  Register #(.width(32)) register_18 (.D(DATA_IN), .en(and_18_out), .clk(CLK), .Q(register_18_q), .clr(1'b0));
  and and_18 (and_18_out, LOAD, decoder_1_out17);
  Register #(.width(32)) register_19 (.D(DATA_IN), .en(and_19_out), .clk(CLK), .Q(register_19_q), .clr(1'b0));
  and and_19 (and_19_out, LOAD, decoder_1_out18);
  Register #(.width(32)) register_20 (.D(DATA_IN), .en(and_20_out), .clk(CLK), .Q(register_20_q), .clr(1'b0));
  and and_20 (and_20_out, LOAD, decoder_1_out19);
  Register #(.width(32)) register_21 (.D(DATA_IN), .en(and_21_out), .clk(CLK), .Q(register_21_q), .clr(1'b0));
  and and_21 (and_21_out, LOAD, decoder_1_out20);
  Register #(.width(32)) register_22 (.D(DATA_IN), .en(and_22_out), .clk(CLK), .Q(register_22_q), .clr(1'b0));
  and and_22 (and_22_out, LOAD, decoder_1_out21);
  Register #(.width(32)) register_23 (.D(DATA_IN), .en(and_23_out), .clk(CLK), .Q(register_23_q), .clr(1'b0));
  and and_23 (and_23_out, LOAD, decoder_1_out22);
  Register #(.width(32)) register_24 (.D(DATA_IN), .en(and_24_out), .clk(CLK), .Q(register_24_q), .clr(1'b0));
  and and_24 (and_24_out, LOAD, decoder_1_out23);
  Register #(.width(32)) register_25 (.D(DATA_IN), .en(and_25_out), .clk(CLK), .Q(register_25_q), .clr(1'b0));
  and and_25 (and_25_out, LOAD, decoder_1_out24);
  Register #(.width(32)) register_26 (.D(DATA_IN), .en(and_26_out), .clk(CLK), .Q(register_26_q), .clr(1'b0));
  and and_26 (and_26_out, LOAD, decoder_1_out25);
  Register #(.width(32)) register_27 (.D(DATA_IN), .en(and_27_out), .clk(CLK), .Q(register_27_q), .clr(1'b0));
  and and_27 (and_27_out, LOAD, decoder_1_out26);
  Register #(.width(32)) register_28 (.D(DATA_IN), .en(and_28_out), .clk(CLK), .Q(register_28_q), .clr(1'b0));
  and and_28 (and_28_out, LOAD, decoder_1_out27);
  Register #(.width(32)) register_29 (.D(DATA_IN), .en(and_29_out), .clk(CLK), .Q(register_29_q), .clr(1'b0));
  and and_29 (and_29_out, LOAD, decoder_1_out28);
  Register #(.width(32)) register_30 (.D(DATA_IN), .en(and_30_out), .clk(CLK), .Q(register_30_q), .clr(1'b0));
  and and_30 (and_30_out, LOAD, decoder_1_out29);
  Register #(.width(32)) register_31 (.D(DATA_IN), .en(and_31_out), .clk(CLK), .Q(register_31_q), .clr(1'b0));
  and and_31 (and_31_out, LOAD, decoder_1_out30);
  Register #(.width(32)) register_32 (.D(DATA_IN), .en(and_32_out), .clk(CLK), .Q(register_32_q), .clr(1'b0));
  and and_32 (and_32_out, LOAD, decoder_1_out31);
  Multiplexer #(.select(5), .width(32), .enable("false")) multiplexer_1 (
    .in0(register_1_q), .in1(register_2_q), .in2(register_3_q), .in3(register_4_q), .in4(register_5_q),
    .in5(register_6_q), .in6(register_7_q), .in7(register_8_q), .in8(register_9_q), .in9(register_10_q),
    .in10(register_11_q), .in11(register_12_q), .in12(register_13_q), .in13(register_14_q),
    .in14(register_15_q), .in15(register_16_q), .in16(register_17_q), .in17(register_18_q),
    .in18(register_19_q), .in19(register_20_q), .in20(register_21_q), .in21(register_22_q),
    .in22(register_23_q), .in23(register_24_q), .in24(register_25_q), .in25(register_26_q),
    .in26(register_27_q), .in27(register_28_q), .in28(register_29_q), .in29(register_30_q),
    .in30(register_31_q), .in31(register_32_q), .out(DATA_A), .sel(ADDR_A));
  Multiplexer #(.select(5), .width(32), .enable("false")) multiplexer_2 (
    .in0(register_1_q), .in1(register_2_q), .in2(register_3_q), .in3(register_4_q), .in4(register_5_q),
    .in5(register_6_q), .in6(register_7_q), .in7(register_8_q), .in8(register_9_q), .in9(register_10_q),
    .in10(register_11_q), .in11(register_12_q), .in12(register_13_q), .in13(register_14_q),
    .in14(register_15_q), .in15(register_16_q), .in16(register_17_q), .in17(register_18_q),
    .in18(register_19_q), .in19(register_20_q), .in20(register_21_q), .in21(register_22_q),
    .in22(register_23_q), .in23(register_24_q), .in24(register_25_q), .in25(register_26_q),
    .in26(register_27_q), .in27(register_28_q), .in28(register_29_q), .in29(register_30_q),
    .in30(register_31_q), .in31(register_32_q), .out(DATA_B), .sel(ADDR_B));
endmodule

module D_MEM (
  input  [3:0] in_1,
  input  [31:0] in_2,
  input  in_3,
  input  [31:0] in_4,
  output [31:0] out_5
);

  wire undriven;
  wire [23:0] bit_extender_1_out;

  RAM #(.addrWidth(24), .dataWidth(32), .databus("bibus")) ram_1 (
    .addr(bit_extender_1_out), .we(undriven), .oe(1'b1), .clk(in_3), .din(in_4), .dout(out_5));
  Bit_Extender #(.in_width(32), .out_width(24), .\type ("zero")) bit_extender_1 (.in(in_2), .out(bit_extender_1_out));

  // Notes on the sheet:
  //   Data
  //   Address
endmodule

module I_MEM (
  input  [31:0] in_1,
  output [31:0] out_2
);

  wire [23:0] bit_extender_1_out;

  ROM #(.addrWidth(24), .dataWidth(32)) rom_1 (.addr(bit_extender_1_out), .data(out_2));
  Bit_Extender #(.in_width(32), .out_width(24), .\type ("zero")) bit_extender_1 (.in(in_1), .out(bit_extender_1_out));
endmodule

module ALU (
  input  [3:0] in_1,
  input  [31:0] in_2,
  input  [31:0] in_3,
  output [31:0] out_4
);

  wire ADD, AND, comparator_1_lt, comparator_2_lt, LUI, multiplexer_4_out, multiplexer_5_out, not_1_out,
       not_2_out, not_3_out, not_4_out, not_5_out, not_6_out, not_7_out, not_8_out, not_9_out, not_10_out,
       not_11_out, not_12_out, not_13_out, not_14_out, not_15_out, not_16_out, not_17_out, not_18_out,
       not_19_out, not_20_out, not_21_out, not_22_out, not_23_out, not_24_out, not_25_out, not_26_out, OR,
       SLL, SLT, SLTU, SRA, SRL, SUB, XOR;
  wire [4:0] bit_extender_1_out;
  wire [31:0] adder_1_out, and_12_out, bit_extender_2_out, bit_extender_3_out, multiplexer_1_out,
       multiplexer_2_out, multiplexer_3_out, multiplexer_6_out, multiplexer_7_out, multiplexer_8_out,
       multiplexer_9_out, multiplexer_10_out, or_1_out, or_2_out, shifter_1_out, shifter_2_out,
       shifter_3_out, subtractor_1_out, xor_1_out;

  not not_1 (not_1_out, in_1[3]);
  not not_2 (not_2_out, in_1[2]);
  not not_3 (not_3_out, in_1[1]);
  not not_4 (not_4_out, in_1[0]);
  not not_5 (not_5_out, in_1[2]);
  not not_6 (not_6_out, in_1[1]);
  not not_7 (not_7_out, in_1[0]);
  not not_8 (not_8_out, in_1[3]);
  not not_9 (not_9_out, in_1[2]);
  not not_10 (not_10_out, in_1[1]);
  not not_11 (not_11_out, in_1[3]);
  not not_12 (not_12_out, in_1[2]);
  not not_13 (not_13_out, in_1[0]);
  not not_14 (not_14_out, in_1[3]);
  not not_15 (not_15_out, in_1[2]);
  not not_16 (not_16_out, in_1[3]);
  not not_17 (not_17_out, in_1[1]);
  not not_18 (not_18_out, in_1[0]);
  not not_19 (not_19_out, in_1[3]);
  not not_20 (not_20_out, in_1[1]);
  not not_21 (not_21_out, in_1[1]);
  not not_22 (not_22_out, in_1[3]);
  not not_23 (not_23_out, in_1[0]);
  not not_24 (not_24_out, in_1[3]);
  not not_25 (not_25_out, in_1[2]);
  not not_26 (not_26_out, in_1[1]);
  and and_1 (ADD, not_1_out, not_2_out, not_3_out, not_4_out);
  and and_2 (SUB, in_1[3], not_5_out, not_6_out, not_7_out);
  and and_3 (SLL, not_8_out, not_9_out, not_10_out, in_1[0]);
  and and_4 (SLT, not_11_out, not_12_out, in_1[1], not_13_out);
  and and_5 (SLTU, not_14_out, not_15_out, in_1[1], in_1[0]);
  and and_6 (XOR, not_16_out, in_1[2], not_17_out, not_18_out);
  and and_7 (SRL, not_19_out, in_1[2], not_20_out, in_1[0]);
  and and_8 (SRA, in_1[3], in_1[2], not_21_out, in_1[0]);
  and and_9 (OR, not_22_out, in_1[2], in_1[1], not_23_out);
  and and_10 (AND, not_24_out, in_1[2], in_1[1], in_1[0]);
  and and_11 (LUI, in_1[3], not_25_out, not_26_out, in_1[0]);
  Bit_Extender #(.in_width(32), .out_width(5), .\type ("zero")) bit_extender_1 (.in(in_3), .out(bit_extender_1_out));
  Adder #(.width(32)) adder_1 (.a(in_2), .b(in_3), .out(adder_1_out), .cin(1'b0));  // open: cout
  Subtractor #(.width(32)) subtractor_1 (.a(in_2), .b(in_3), .out(subtractor_1_out), .bin(1'b0));  // open: bout
  Shifter #(.width(32)) shifter_1 (.in(in_2), .\dist (bit_extender_1_out), .out(shifter_1_out));
  Comparator #(.width(32)) comparator_1 (.a(in_2), .b(in_3), .lt(comparator_1_lt));  // open: gt, eq
  Comparator #(.width(32), .mode("unsigned")) comparator_2 (.a(in_2), .b(in_3), .lt(comparator_2_lt));  // open: gt, eq
  assign xor_1_out = in_2 ^ in_3;  // XOR_Gate xor_1, 32 bits wide
  Shifter #(.width(32), .shift("lr")) shifter_2 (.in(in_2), .\dist (bit_extender_1_out), .out(shifter_2_out));
  Shifter #(.width(32), .shift("ar")) shifter_3 (.in(in_2), .\dist (bit_extender_1_out), .out(shifter_3_out));
  assign or_1_out = in_2 | in_3;  // OR_Gate or_1, 32 bits wide
  assign and_12_out = in_2 & in_3;  // AND_Gate and_12, 32 bits wide
  Multiplexer #(.width(32), .enable("false")) multiplexer_1 (
    .in0({32{1'b0}}), .in1(adder_1_out), .out(multiplexer_1_out), .sel(ADD));
  Multiplexer #(.width(32), .enable("false")) multiplexer_2 (
    .in0({32{1'b0}}), .in1(subtractor_1_out), .out(multiplexer_2_out), .sel(SUB));
  Multiplexer #(.width(32), .enable("false")) multiplexer_3 (
    .in0({32{1'b0}}), .in1(shifter_1_out), .out(multiplexer_3_out), .sel(SLL));
  Multiplexer #(.enable("false")) multiplexer_4 (.in0(1'b0), .in1(comparator_1_lt), .out(multiplexer_4_out), .sel(SLT));
  Multiplexer #(.enable("false")) multiplexer_5 (
    .in0(1'b0), .in1(comparator_2_lt), .out(multiplexer_5_out), .sel(SLTU));
  Multiplexer #(.width(32), .enable("false")) multiplexer_6 (
    .in0({32{1'b0}}), .in1(xor_1_out), .out(multiplexer_6_out), .sel(XOR));
  Multiplexer #(.width(32), .enable("false")) multiplexer_7 (
    .in0({32{1'b0}}), .in1(shifter_2_out), .out(multiplexer_7_out), .sel(SRL));
  Multiplexer #(.width(32), .enable("false")) multiplexer_8 (
    .in0({32{1'b0}}), .in1(shifter_3_out), .out(multiplexer_8_out), .sel(SRA));
  Multiplexer #(.width(32), .enable("false")) multiplexer_9 (
    .in0({32{1'b0}}), .in1(or_1_out), .out(multiplexer_9_out), .sel(OR));
  Multiplexer #(.width(32), .enable("false")) multiplexer_10 (
    .in0({32{1'b0}}), .in1(and_12_out), .out(multiplexer_10_out), .sel(AND));
  assign bit_extender_2_out = {{31{1'b0}}, multiplexer_4_out};  // Bit_Extender bit_extender_2
  assign bit_extender_3_out = {{31{1'b0}}, multiplexer_5_out};  // Bit_Extender bit_extender_3
  assign or_2_out = multiplexer_1_out | multiplexer_2_out | multiplexer_3_out | bit_extender_2_out | bit_extender_3_out | multiplexer_6_out | multiplexer_7_out | multiplexer_8_out | multiplexer_9_out | multiplexer_10_out;  // OR_Gate or_2, 32 bits wide
  Multiplexer #(.width(32), .enable("false")) multiplexer_11 (.in0(or_2_out), .in1(in_3), .out(out_4), .sel(LUI));
endmodule

module ImmGen (
  input  [5:0] in_1,
  input  [24:0] in_2,
  output [31:0] out_3
);

  wire [1:0] undriven;
  wire [6:0] multiplexer_1_out;
  wire [11:0] multiplexer_2_out;

  Multiplexer #(.width(7), .enable("false")) multiplexer_1 (
    .in0(in_2[24:18]), .in1({7{1'b0}}), .out(multiplexer_1_out));  // open: sel
  Multiplexer #(.select(2), .width(12), .enable("false")) multiplexer_2 (
    .in0({multiplexer_1_out, in_2[17:13]}), .in1({in_2[24:18], in_2[4:0]}), .in2({12{1'b0}}),
    .in3({12{1'b0}}), .out(multiplexer_2_out), .sel(undriven));
  assign out_3 = {{20{multiplexer_2_out[11]}}, multiplexer_2_out};  // Bit_Extender bit_extender_1
endmodule

module BranchCom (
  input  [31:0] in_1,
  input  [31:0] in_2,
  input  BrUn,
  output BrEq,
  output BrLT
);

  wire comparator_1_lt, comparator_2_lt;

  Comparator #(.width(32)) comparator_1 (.a(in_1), .b(in_2), .eq(BrEq), .lt(comparator_1_lt));  // open: gt
  Comparator #(.width(32), .mode("unsigned")) comparator_2 (.a(in_1), .b(in_2), .lt(comparator_2_lt));  // open: gt, eq
  Multiplexer #(.enable("false")) multiplexer_1 (.in0(comparator_1_lt), .in1(comparator_2_lt), .out(BrLT), .sel(BrUn));

  // Notes on the sheet:
  //   Signed
  //   Unsigned
endmodule
